# Fritzing sketch array1 (saved by Fritzing 0.8.7b)
breadboards: 1

parts:
  Part2 = Arduino Leonardo (Rev3b)
  J1 = female pin header, 2 pins [form="♀ (female)"]
  J2 = female pin header, 2 pins [form="♀ (female)"]
  J3 = female pin header, 2 pins [form="♀ (female)"]  # not connected
  J4 = female pin header, 2 pins [form="♀ (female)"]  # not connected
  J5 = female pin header, 2 pins [form="♀ (female)"]  # not connected
  J6 = female pin header, 2 pins [form="♀ (female)"]  # not connected
  J7 = female pin header, 2 pins [form="♀ (female)"]  # not connected
  J8 = female pin header, 2 pins [form="♀ (female)"]  # not connected
  J9 = female pin header, 2 pins [form="♀ (female)"]
  U4 = 74HC4051 [package=so16]
  U5 = 74HC4051 [package=so16]

nets:
  N1: Part2.D2/SDA, U4.C
  N2: Part2.D3_PWM/SCL, U4.B
  N3: Part2.D4/A6, U4.A
  N4: Part2.D5_PWM, U5.C
  N5: Part2.D6_PWM/A7, U5.B
  N6: Part2.D7, U5.A
  VDD: Part2.3V3, U4.VDD, U5.VDD
  VSS: Part2.GND, J9.pin2, U4.VSS, U5.VSS
  N7: J1.pin1, U5.IO1
  N8: J1.pin2, U5.IO0
  N9: J2.pin1, U5.IO3
  N10: J2.pin2, U5.IO2
